// Logisim project schem.circ as structural Verilog: 1 circuit, main circuit main
module main (
);

  wire clk_out, j_k_ff_1_q, j_k_ff_2_q, j_k_ff_2_qn, j_k_ff_3_q, j_k_ff_3_qn, NOR1_out, NOR2_out;

  Button clk (.out(clk_out));
  nor NOR1 (NOR1_out, j_k_ff_2_q, j_k_ff_3_q);
  J_K_Flip_Flop j_k_ff_1 (.J(NOR1_out), .clk(clk_out), .K(1'b1), .Q(j_k_ff_1_q));  // open: Qn, preset, en, reset
  LED Q2 (.in(j_k_ff_1_q));
  nor NOR2 (NOR2_out, j_k_ff_1_q, j_k_ff_3_qn);
  LED Q1 (.in(j_k_ff_2_q));
  LED Q0 (.in(j_k_ff_3_q));
  J_K_Flip_Flop j_k_ff_2 (
    .J(NOR2_out), .clk(clk_out), .K(j_k_ff_3_qn), .Q(j_k_ff_2_q), .Qn(j_k_ff_2_qn));  // open: preset, en, reset
  J_K_Flip_Flop j_k_ff_3 (
    .J(j_k_ff_2_qn), .clk(clk_out), .K(j_k_ff_2_q), .Q(j_k_ff_3_q), .Qn(j_k_ff_3_qn));  // open: preset, en, reset
endmodule
