// Logisim project schem2.circ as structural Verilog: 1 circuit, main circuit main
module main (
);

  wire clk_out, d_ff_1_q, d_ff_2_q, d_ff_2_qn, d_ff_3_q, d_ff_3_qn, NOR1_out, NOR2_out;

  Button clk (.out(clk_out));
  nor NOR1 (NOR1_out, d_ff_2_q, d_ff_3_q);
  D_Flip_Flop d_ff_1 (.clk(clk_out), .D(NOR1_out), .Q(d_ff_1_q));  // open: Qn, preset, en, reset
  LED Q2 (.in(d_ff_1_q));
  LED Q1 (.in(d_ff_2_q));
  nor NOR2 (NOR2_out, d_ff_1_q, d_ff_3_qn);
  LED Q0 (.in(d_ff_3_q));
  D_Flip_Flop d_ff_2 (.clk(clk_out), .D(NOR2_out), .Q(d_ff_2_q), .Qn(d_ff_2_qn));  // open: preset, en, reset
  D_Flip_Flop d_ff_3 (.clk(clk_out), .D(d_ff_2_qn), .Q(d_ff_3_q), .Qn(d_ff_3_qn));  // open: preset, en, reset
endmodule
