// Logisim project schem2v2.circ as structural Verilog: 1 circuit, main circuit main
module main (
);

  wire clk_out, j_k_ff_1_q, j_k_ff_2_q, j_k_ff_2_qn, j_k_ff_3_q, j_k_ff_3_qn, j_k_ff_4_q, j_k_ff_4_qn,
       j_k_ff_5_q, j_k_ff_5_qn, mode_out, NAND1_out, NAND2_out, NAND3_out, not_1_out, not_2_out, XOR1_out,
       XOR2_out, XOR3_out;

  Button mode (.out(mode_out));
  Button clk (.out(clk_out));
  J_K_Flip_Flop j_k_ff_1 (.J(1'b1), .clk(mode_out), .K(1'b1), .Q(j_k_ff_1_q));  // open: Qn, preset, en, reset
  LED Q3 (.in(j_k_ff_5_qn));
  LED Q2 (.in(j_k_ff_4_qn));
  xor XOR2 (XOR2_out, clk_out, XOR3_out);
  LED Q0 (.in(j_k_ff_2_qn));
  LED Q1 (.in(j_k_ff_3_qn));
  J_K_Flip_Flop j_k_ff_2 (
    .J(1'b1), .clk(XOR2_out), .K(1'b1), .Q(j_k_ff_2_q), .Qn(j_k_ff_2_qn), .reset(XOR3_out));  // open: preset, en
  J_K_Flip_Flop j_k_ff_3 (
    .J(1'b1), .clk(j_k_ff_2_q), .K(1'b1), .Q(j_k_ff_3_q), .Qn(j_k_ff_3_qn), .reset(XOR3_out));  // open: preset, en
  not not_1 (not_1_out, j_k_ff_1_q);
  nand NAND2 (NAND2_out, j_k_ff_5_qn, j_k_ff_3_qn, j_k_ff_2_qn, j_k_ff_1_q);
  nand NAND1 (NAND1_out, not_1_out, j_k_ff_4_qn, j_k_ff_5_q);
  J_K_Flip_Flop j_k_ff_4 (
    .J(1'b1), .clk(j_k_ff_3_q), .K(1'b1), .Q(j_k_ff_4_q), .Qn(j_k_ff_4_qn), .reset(XOR3_out));  // open: preset, en
  not not_2 (not_2_out, NAND2_out);
  nand NAND3 (NAND3_out, not_2_out, j_k_ff_4_q);
  J_K_Flip_Flop j_k_ff_5 (
    .J(1'b1), .clk(j_k_ff_4_q), .K(1'b1), .Q(j_k_ff_5_q), .Qn(j_k_ff_5_qn), .reset(XOR3_out));  // open: preset, en
  xor XOR1 (XOR1_out, NAND3_out, NAND1_out);
  xor XOR3 (XOR3_out, mode_out, XOR1_out);
endmodule
