// Logisim project schem.circ as structural Verilog: 1 circuit, main circuit main
module main (
  input  E
);

  wire and_1_out, and_2_out, and_3_out, and_4_out, and_5_out, and_6_out, and_7_out, and_8_out, inp0_out,
       inp1_out, inp2_out, nand_1_out, nand_2_out, nand_3_out, nor_1_out, nor_2_out, nor_3_out, nor_4_out,
       nor_5_out, nor_6_out, nor_7_out, nor_8_out, not_1_out, not_2_out, not_3_out, not_4_out, not_5_out,
       not_6_out, not_7_out, not_8_out, not_9_out, READ_out, RESET_out, s_r_ff_1_q, s_r_ff_2_q, s_r_ff_3_q,
       s_r_ff_3_qn, START_out;

  Button READ (.out(READ_out));
  Button inp2 (.out(inp2_out));
  Button inp1 (.out(inp1_out));
  Button inp0 (.out(inp0_out));
  Button START (.out(START_out));
  Button RESET (.out(RESET_out));
  and and_1 (and_1_out, READ_out, E);
  and and_2 (and_2_out, inp2_out, E);
  and and_3 (and_3_out, s_r_ff_1_q, inp0_out);
  and and_4 (and_4_out, START_out, s_r_ff_3_qn);
  S_R_Flip_Flop s_r_ff_1 (.Q(s_r_ff_1_q), .reset(not_2_out), .preset(not_1_out));  // open: S, R, clk, Qn
  nor nor_1 (nor_1_out, RESET_out, s_r_ff_2_q);
  nor nor_2 (nor_2_out, RESET_out, inp0_out);
  nor nor_3 (nor_3_out, and_1_out, and_2_out);
  nand nand_1 (nand_1_out, E, inp1_out);
  nor nor_4 (nor_4_out, and_3_out, and_4_out);
  not not_1 (not_1_out, nor_4_out);
  not not_2 (not_2_out, nor_1_out);
  not not_3 (not_3_out, nor_2_out);
  LED led_1 (.in(s_r_ff_1_q));
  not not_4 (not_4_out, nor_3_out);
  nand nand_2 (nand_2_out, nor_3_out, nand_1_out);
  and and_5 (and_5_out, nand_2_out, s_r_ff_1_q);
  and and_6 (and_6_out, inp1_out, s_r_ff_2_q);
  nor nor_5 (nor_5_out, not_3_out, s_r_ff_3_q);
  nor nor_6 (nor_6_out, and_5_out, and_6_out);
  not not_5 (not_5_out, nor_6_out);
  S_R_Flip_Flop s_r_ff_2 (.Q(s_r_ff_2_q), .reset(not_6_out), .preset(not_5_out));  // open: S, R, clk, Qn
  not not_6 (not_6_out, nor_5_out);
  LED led_2 (.in(s_r_ff_2_q));
  and and_7 (and_7_out, not_4_out, s_r_ff_2_q);
  and and_8 (and_8_out, inp2_out, s_r_ff_3_q);
  S_R_Flip_Flop s_r_ff_3 (.Q(s_r_ff_3_q), .reset(not_7_out), .Qn(s_r_ff_3_qn), .preset(not_8_out));  // open: S, R, clk
  nor nor_7 (nor_7_out, not_3_out, inp1_out);
  not not_7 (not_7_out, nor_7_out);
  nor nor_8 (nor_8_out, and_7_out, and_8_out);
  not not_8 (not_8_out, nor_8_out);
  LED led_3 (.in(s_r_ff_3_q));
  nand nand_3 (nand_3_out, READ_out, s_r_ff_3_q);
  LED led_4 (.in(not_9_out));
  not not_9 (not_9_out, nand_3_out);
endmodule
